// Logisim project Clackertron_sync.circ as structural Verilog: 16 circuits, main circuit main
module main (
  input  in_1,
  input  in_2,
  input  in_3,
  input  A,
  input  B,
  input  CI,
  output S,
  output CO
);

  wire half_add_2_c, half_add_2_s, half_add_3_c, single_read_latch_1_q, spdt_co_1_c1;

  D_Flip_Flop d_ff_1 ();  // open: D, clk, Q, Qn, preset, reset
  D_Latch d_latch_1 ();  // open: CLK, EN, D, Q, nQ
  D_Register d_register_1 ();  // open: D, CLK, EN_ovd, EN_pg, Q, nQ, FB
  LED led_1 (.in(spdt_co_1_c1));
  SPDT_CO spdt_co_1 (
    .coil_L(in_2), .coil_R(1'b0), .CLK(in_1), .NO1(single_read_latch_1_q), .C1(spdt_co_1_c1));  // open: NC1
  single_read_latch single_read_latch_1 (
    .D(in_3), .OE(in_2), .CLK(in_1), .FB(single_read_latch_1_q), .Q(single_read_latch_1_q));
  Half_Add half_add_1 ();  // open: CLK, A, B, C, S, nS
  Full_Add full_add_1 ();  // open: B, nB, A, CLK, CI, S, CO
  ADD add_1 ();  // open: CLK, CI, A, B, nB, S, CO
  Half_Add half_add_2 (.A(A), .B(B), .C(half_add_2_c), .S(half_add_2_s));  // open: CLK, nS
  MUX mux_1 ();  // open: S, CLK, A, B, out_5
  DEMUX demux_1 ();  // open: in_1, S, CLK, A, B
  D_Register d_register_2 ();  // open: D, CLK, EN_ovd, EN_pg, Q, nQ, FB
  INC inc_1 ();  // open: A, CLK, CI, nS, CO, S
  Half_Add half_add_3 (.A(half_add_2_s), .B(CI), .C(half_add_3_c), .S(S));  // open: CLK, nS
  or or_1 (CO, half_add_3_c, half_add_2_c);
  INC_DEC inc_dec_1 ();  // open: CLK, CI, D, IE, DEC, OE, S, CO
  ADD_SUB add_sub_1 ();  // open: CLK, A, nA, B, nB, CI, s_SUB, s_ADD, S, CO, OA

  // Notes on the sheet:
  //   FA old
endmodule

module single_read_latch (
  input  D,
  input  OE,
  input  CLK,
  input  FB,
  output Q
);

  wire and_1_out, hiz_detector_1_out_2, not_1_out, t_ff_1_q, t_ff_2_q;

  HiZ_Detector hiz_detector_1 (.in_1(FB), .out_2(hiz_detector_1_out_2));
  not not_1 (not_1_out, OE);
  T_Flip_Flop #(.trigger("falling")) t_ff_1 (
    .T(1'b1), .clk(and_1_out), .Q(t_ff_1_q), .reset(not_1_out));  // open: Qn, preset
  and and_1 (and_1_out, CLK, ~hiz_detector_1_out_2);  // AND_Gate
  T_Flip_Flop #(.trigger("falling")) t_ff_2 (
    .T(1'b1), .clk(t_ff_1_q), .Q(t_ff_2_q), .reset(not_1_out));  // open: Qn, preset
  D_Flip_Flop #(.trigger("low")) d_ff_1 (.D(D), .clk(OE), .Q(Q), .reset(t_ff_2_q));  // open: Qn, preset

  // Notes on the sheet:
  //   OE high -> enables "current flow" of Capacitor
  //   FB  HiZ  -> halts "current flow" of Capacitor
  //   Capacitor emulation as a delay unit
endmodule

module double_read_latch (
  input  D,
  input  OE,
  input  CLK,
  input  FB,
  output Q
);

  wire and_1_out, hiz_detector_1_out_2, not_1_out, t_ff_1_q, t_ff_2_q, t_ff_3_q;

  HiZ_Detector hiz_detector_1 (.in_1(FB), .out_2(hiz_detector_1_out_2));
  not not_1 (not_1_out, OE);
  T_Flip_Flop #(.trigger("falling")) t_ff_1 (
    .T(1'b1), .clk(and_1_out), .Q(t_ff_1_q), .reset(not_1_out));  // open: Qn, preset
  and and_1 (and_1_out, CLK, ~hiz_detector_1_out_2);  // AND_Gate
  T_Flip_Flop #(.trigger("falling")) t_ff_2 (
    .T(1'b1), .clk(t_ff_1_q), .Q(t_ff_2_q), .reset(not_1_out));  // open: Qn, preset
  T_Flip_Flop #(.trigger("falling")) t_ff_3 (
    .T(1'b1), .clk(t_ff_2_q), .Q(t_ff_3_q), .reset(not_1_out));  // open: Qn, preset
  D_Flip_Flop #(.trigger("low")) d_ff_1 (.D(D), .clk(OE), .Q(Q), .reset(t_ff_3_q));  // open: Qn, preset

  // Notes on the sheet:
  //   OE high -> enables "current flow" of Capacitor
  //   FB  HiZ  -> halts "current flow" of Capacitor
  //   Capacitor emulation as a delay unit
endmodule

module single_read_latch_8 (
  input  [7:0] D,
  input  CLK,
  input  OE,
  input  FB,
  output [7:0] Q
);

  single_read_latch single_read_latch_1 (.D(D[0]), .OE(OE), .CLK(CLK), .FB(FB), .Q(Q[0]));
  single_read_latch single_read_latch_2 (.D(D[1]), .OE(OE), .CLK(CLK), .FB(FB), .Q(Q[1]));
  single_read_latch single_read_latch_3 (.D(D[2]), .OE(OE), .CLK(CLK), .FB(FB), .Q(Q[2]));
  single_read_latch single_read_latch_4 (.D(D[3]), .OE(OE), .CLK(CLK), .FB(FB), .Q(Q[3]));
  single_read_latch single_read_latch_5 (.D(D[4]), .OE(OE), .CLK(CLK), .FB(FB), .Q(Q[4]));
  single_read_latch single_read_latch_6 (.D(D[5]), .OE(OE), .CLK(CLK), .FB(FB), .Q(Q[5]));
  single_read_latch single_read_latch_7 (.D(D[6]), .OE(OE), .CLK(CLK), .FB(FB), .Q(Q[6]));
  single_read_latch single_read_latch_8 (.D(D[7]), .OE(OE), .CLK(CLK), .FB(FB), .Q(Q[7]));
endmodule

module D_Latch (
  input  CLK,
  input  EN,
  input  D,
  output Q,
  output nQ
);

  wire and_1_out, spdt_ci_1_no1;

  SPDT_CI spdt_ci_1 (.coil_L(EN), .coil_R(1'b0), .CLK(CLK), .C1(D), .NO1(spdt_ci_1_no1));  // open: NC1
  D_Flip_Flop d_ff_1 (.D(spdt_ci_1_no1), .clk(and_1_out), .Q(Q), .Qn(nQ));  // open: preset, reset
  and and_1 (and_1_out, CLK, EN);

  // Notes on the sheet:
  //   max CLK = 2
endmodule

module D_Register (
  input  [7:0] D,
  input  CLK,
  input  EN_ovd,
  input  EN_pg,
  output [7:0] Q,
  output [7:0] nQ,
  output FB
);

  wire and_1_out, or_1_out, single_read_latch_1_q, spdt_co_1_c1, undriven;
  wire [7:0] mux_1_out_5;

  single_read_latch single_read_latch_1 (.D(1'b1), .OE(EN_pg), .CLK(CLK), .FB(FB), .Q(single_read_latch_1_q));
  SPDT_CO spdt_co_1 (
    .coil_L(1'b0), .coil_R(EN_pg), .CLK(CLK), .NC1(1'b0), .NO1(single_read_latch_1_q), .C1(spdt_co_1_c1));
  Pull_Resistor pull_resistor_1 (.node(spdt_co_1_c1));
  MUX mux_1 (.S(or_1_out), .CLK(CLK), .B(D), .out_5(mux_1_out_5));  // open: A
  or or_1 (or_1_out, EN_ovd, spdt_co_1_c1);
  D_Flip_Flop d_ff_1 (.D(mux_1_out_5[0]), .clk(and_1_out), .Q(Q[0]), .Qn(nQ[0]));  // open: preset, reset
  D_Flip_Flop d_ff_2 (.D(mux_1_out_5[1]), .clk(and_1_out), .Q(Q[1]), .Qn(nQ[1]));  // open: preset, reset
  D_Flip_Flop d_ff_3 (.D(mux_1_out_5[2]), .clk(and_1_out), .Q(Q[2]), .Qn(nQ[2]));  // open: preset, reset
  D_Flip_Flop d_ff_4 (.D(mux_1_out_5[3]), .clk(and_1_out), .Q(Q[3]), .Qn(nQ[3]));  // open: preset, reset
  D_Flip_Flop d_ff_5 (.D(mux_1_out_5[4]), .clk(and_1_out), .Q(Q[4]), .Qn(nQ[4]));  // open: preset, reset
  D_Flip_Flop d_ff_6 (.D(mux_1_out_5[5]), .clk(and_1_out), .Q(Q[5]), .Qn(nQ[5]));  // open: preset, reset
  D_Flip_Flop d_ff_7 (.D(mux_1_out_5[6]), .clk(and_1_out), .Q(Q[6]), .Qn(nQ[6]));  // open: preset, reset
  D_Flip_Flop d_ff_8 (.D(mux_1_out_5[7]), .clk(and_1_out), .Q(Q[7]), .Qn(nQ[7]));  // open: preset, reset
  and and_1 (and_1_out, CLK, or_1_out);
  SPDT_CO spdt_co_2 (.coil_L(or_1_out), .coil_R(1'b0), .CLK(CLK), .NC1(undriven), .NO1(1'b1), .C1(FB));
  // NoConnect on undriven

  // Notes on the sheet:
  //   max CLK = 2
  //   feed back signal for "current" based devices
  //   is non HiZ iff D is directly connected to the D-Latches
endmodule

module Half_Add (
  input  CLK,
  input  A,
  input  B,
  output S,
  output nS,
  output C
);

  DPDT_CICO dpdt_cico_1 (.coil_L(A), .coil_R(B), .CLK(CLK), .C1(1'b1), .NC2(B), .NO2(1'b0), .C2(C), .NC1(nS), .NO1(S));

  // Notes on the sheet:
  //   Half Adder Relay equivalent
endmodule

module Full_Add (
  input  B,
  input  nB,
  input  A,
  input  CI,
  input  CLK,
  output S,
  output CO
);

  DPDT_COCO dpdt_coco_1 (.coil_L(CI), .coil_R(A), .CLK(CLK), .NC1(A), .NO1(B), .NC2(B), .NO2(nB), .C1(CO), .C2(S));
endmodule

module ADD (
  input  CLK,
  input  CI,
  input  [7:0] A,
  input  [7:0] B,
  input  [7:0] nB,
  output [7:0] S,
  output CO
);

  wire full_add_1_co, full_add_2_co, full_add_3_co, full_add_4_co, full_add_5_co, full_add_6_co,
       full_add_7_co;

  Full_Add full_add_1 (.B(B[0]), .nB(nB[0]), .A(A[0]), .CLK(CLK), .CI(CI), .S(S[0]), .CO(full_add_1_co));
  Full_Add full_add_2 (.B(B[1]), .nB(nB[1]), .A(A[1]), .CLK(CLK), .CI(full_add_1_co), .S(S[1]), .CO(full_add_2_co));
  Full_Add full_add_3 (.B(B[2]), .nB(nB[2]), .A(A[2]), .CLK(CLK), .CI(full_add_2_co), .S(S[2]), .CO(full_add_3_co));
  Full_Add full_add_4 (.B(B[3]), .nB(nB[3]), .A(A[3]), .CLK(CLK), .CI(full_add_3_co), .S(S[3]), .CO(full_add_4_co));
  Full_Add full_add_5 (.B(B[4]), .nB(nB[4]), .A(A[4]), .CLK(CLK), .CI(full_add_4_co), .S(S[4]), .CO(full_add_5_co));
  Full_Add full_add_6 (.B(B[5]), .nB(nB[5]), .A(A[5]), .CLK(CLK), .CI(full_add_5_co), .S(S[5]), .CO(full_add_6_co));
  Full_Add full_add_7 (.B(B[6]), .nB(nB[6]), .A(A[6]), .CLK(CLK), .CI(full_add_6_co), .S(S[6]), .CO(full_add_7_co));
  Full_Add full_add_8 (.B(B[7]), .nB(nB[7]), .A(A[7]), .CLK(CLK), .CI(full_add_7_co), .S(S[7]), .CO(CO));

  // Notes on the sheet:
  //   max CLK = 8
endmodule

module ADD_SUB (
  input  CLK,
  input  [7:0] A,
  input  [7:0] nA,
  input  [7:0] B,
  input  [7:0] nB,
  input  CI,
  input  s_SUB,
  input  s_ADD,
  output [7:0] S,
  output CO,
  output OA
);

  wire add_1_co;
  wire [7:0] mux_1_out_5;

  MUX mux_1 (.S(s_SUB), .CLK(CLK), .A(A), .B(nA), .out_5(mux_1_out_5));
  ADD add_1 (.CLK(CLK), .CI(CI), .A(mux_1_out_5), .B(B), .nB(nB), .S(S), .CO(add_1_co));
  SPDT_CO spdt_co_1 (.coil_L(add_1_co), .coil_R(1'b0), .CLK(CLK), .NC1(s_SUB), .NO1(s_ADD), .C1(CO));
  or or_1 (OA, s_SUB, s_ADD);

  // Notes on the sheet:
  //   Relay logic invalid for ~SUB & ~ADD
  //   Output Available
endmodule

module MUX (
  input  [7:0] A,
  input  S,
  input  CLK,
  input  [7:0] B,
  output [7:0] out_5
);

  DPDT_COCO dpdt_coco_1 (
    .coil_L(S), .coil_R(1'b0), .CLK(CLK), .NC1(A[0]), .NO1(B[0]), .NC2(A[1]), .NO2(B[1]), .C1(out_5[0]),
    .C2(out_5[1]));
  DPDT_COCO dpdt_coco_2 (
    .coil_L(S), .coil_R(1'b0), .CLK(CLK), .NC1(A[2]), .NO1(B[2]), .NC2(A[3]), .NO2(B[3]), .C1(out_5[2]),
    .C2(out_5[3]));
  DPDT_COCO dpdt_coco_3 (
    .coil_L(S), .coil_R(1'b0), .CLK(CLK), .NC1(A[4]), .NO1(B[4]), .NC2(A[5]), .NO2(B[5]), .C1(out_5[4]),
    .C2(out_5[5]));
  DPDT_COCO dpdt_coco_4 (
    .coil_L(S), .coil_R(1'b0), .CLK(CLK), .NC1(A[6]), .NO1(B[6]), .NC2(A[7]), .NO2(B[7]), .C1(out_5[6]),
    .C2(out_5[7]));
endmodule

module DEMUX (
  input  [7:0] in_1,
  input  S,
  input  CLK,
  output [7:0] A,
  output [7:0] B
);

  DPDT_CICI dpdt_cici_1 (
    .coil_L(S), .coil_R(1'b0), .CLK(CLK), .C1(in_1[0]), .C2(in_1[1]), .NC1(A[0]), .NO1(B[0]), .NC2(A[1]),
    .NO2(B[1]));
  DPDT_CICI dpdt_cici_2 (
    .coil_L(S), .coil_R(1'b0), .CLK(CLK), .C1(in_1[2]), .C2(in_1[3]), .NC1(A[2]), .NO1(B[2]), .NC2(A[3]),
    .NO2(B[3]));
  DPDT_CICI dpdt_cici_3 (
    .coil_L(S), .coil_R(1'b0), .CLK(CLK), .C1(in_1[4]), .C2(in_1[5]), .NC1(A[4]), .NO1(B[4]), .NC2(A[5]),
    .NO2(B[5]));
  DPDT_CICI dpdt_cici_4 (
    .coil_L(S), .coil_R(1'b0), .CLK(CLK), .C1(in_1[6]), .C2(in_1[7]), .NC1(A[6]), .NO1(B[6]), .NC2(A[7]),
    .NO2(B[7]));
endmodule

module INC (
  input  CLK,
  input  CI,
  input  [7:0] A,
  output [7:0] S,
  output [7:0] nS,
  output CO
);

  wire half_add_1_c, half_add_2_c, half_add_3_c, half_add_4_c, half_add_5_c, half_add_6_c, or_1_out;

  or or_1 (or_1_out, CI, A[0]);
  SPDT_CI spdt_ci_1 (.coil_L(A[0]), .coil_R(CI), .CLK(CLK), .C1(1'b1), .NC1(S[0]), .NO1(nS[0]));
  Half_Add half_add_1 (.CLK(CLK), .A(or_1_out), .B(A[1]), .C(half_add_1_c), .S(S[1]), .nS(nS[1]));
  Half_Add half_add_2 (.CLK(CLK), .A(half_add_1_c), .B(A[2]), .C(half_add_2_c), .S(S[2]), .nS(nS[2]));
  Half_Add half_add_3 (.CLK(CLK), .A(half_add_2_c), .B(A[3]), .C(half_add_3_c), .S(S[3]), .nS(nS[3]));
  Half_Add half_add_4 (.CLK(CLK), .A(half_add_3_c), .B(A[4]), .C(half_add_4_c), .S(S[4]), .nS(nS[4]));
  Half_Add half_add_5 (.CLK(CLK), .A(half_add_4_c), .B(A[5]), .C(half_add_5_c), .S(S[5]), .nS(nS[5]));
  Half_Add half_add_6 (.CLK(CLK), .A(half_add_5_c), .B(A[6]), .C(half_add_6_c), .S(S[6]), .nS(nS[6]));
  Half_Add half_add_7 (.CLK(CLK), .A(half_add_6_c), .B(A[7]), .C(CO), .S(S[7]), .nS(nS[7]));

  // Notes on the sheet:
  //   max CLK = 7
endmodule

module INC_DEC (
  input  CLK,
  input  CI,
  input  [7:0] D,
  input  IE,
  input  DEC,
  input  OE,
  output [7:0] S,
  output CO
);

  wire d_latch_1_nq, d_latch_1_q, inc_1_co, spdt_ci_1_nc1;
  wire [7:0] d_register_1_nq, d_register_1_q, inc_1_ns, inc_1_s, mux_1_out_5, mux_2_out_5;

  D_Latch d_latch_1 (.CLK(CLK), .EN(IE), .D(CI), .Q(d_latch_1_q), .nQ(d_latch_1_nq));
  D_Register d_register_1 (.D(D), .CLK(CLK), .EN_ovd(IE), .Q(d_register_1_q), .nQ(d_register_1_nq));  // open: EN_pg, FB
  // NoConnect on d_latch_1_nq
  MUX mux_1 (.S(DEC), .CLK(CLK), .A(d_register_1_q), .B(d_register_1_nq), .out_5(mux_1_out_5));
  INC inc_1 (.A(mux_1_out_5), .CLK(CLK), .CI(d_latch_1_q), .nS(inc_1_ns), .CO(inc_1_co), .S(inc_1_s));
  MUX mux_2 (.S(DEC), .CLK(CLK), .A(inc_1_s), .B(inc_1_ns), .out_5(mux_2_out_5));
  SPDT_CI spdt_ci_1 (.coil_L(1'b0), .coil_R(OE), .CLK(CLK), .C1(inc_1_co), .NC1(spdt_ci_1_nc1), .NO1(CO));
  MUX mux_3 (.S(OE), .CLK(CLK), .B(mux_2_out_5), .out_5(S));  // open: A
  // NoConnect on spdt_ci_1_nc1

  // Notes on the sheet:
  //   output must not feedback input
endmodule

module LU (
  input  [7:0] A,
  input  [7:0] nA,
  input  [7:0] B,
  input  [7:0] nB,
  input  s_A,
  input  s_OR,
  input  s_XOR,
  input  s_AND,
  input  s_NEG,
  input  CI,
  input  s_ROR,
  input  s_ROL,
  input  s_LSR,
  input  s_ASL
);
endmodule

module PC (
  input  [7:0] AD_BUS_I,
  input  [7:0] D_BUS_I,
  input  s_BUS_SEL,
  input  CI,
  input  s_inc,
  input  s_in,
  input  s_out,
  input  CLK,
  output [7:0] AD_BUS_O,
  output [7:0] D_BUS_O,
  output CO
);

  wire d_register_1_fb;
  wire [3:0] d_register_1_q, d_register_1_q_2, inc_1_s, inc_1_s_2, mux_2_out_5, mux_2_out_5_2;
  wire [7:0] demux_1_b, mux_1_out_5, single_read_latch_8_1_q;

  MUX mux_1 (.S(s_BUS_SEL), .CLK(CLK), .A(AD_BUS_I), .B(D_BUS_I), .out_5(mux_1_out_5));
  Hex_Digit_Display #(.decimalPoint("false")) hex_digit_display_1 (.value(inc_1_s_2));
  Hex_Digit_Display #(.decimalPoint("false")) hex_digit_display_2 (.value(inc_1_s));
  INC inc_1 (
    .A({d_register_1_q_2, d_register_1_q}), .CLK(CLK), .CI(CI), .CO(CO), .S({inc_1_s_2, inc_1_s}));  // open: nS
  single_read_latch_8 single_read_latch_8_1 (
    .D({inc_1_s_2, inc_1_s}), .CLK(CLK), .OE(s_inc), .FB(d_register_1_fb), .Q(single_read_latch_8_1_q));
  Hex_Digit_Display #(.decimalPoint("false")) hex_digit_display_3 (.value(mux_2_out_5_2));
  MUX mux_2 (.S(s_inc), .CLK(CLK), .A(mux_1_out_5), .B(single_read_latch_8_1_q), .out_5({mux_2_out_5_2, mux_2_out_5}));
  Hex_Digit_Display #(.decimalPoint("false")) hex_digit_display_4 (.value(mux_2_out_5));
  Hex_Digit_Display #(.decimalPoint("false")) hex_digit_display_5 (.value(d_register_1_q_2));
  D_Register d_register_1 (
    .D({mux_2_out_5_2, mux_2_out_5}), .CLK(CLK), .EN_ovd(s_in), .EN_pg(s_inc),
    .Q({d_register_1_q_2, d_register_1_q}), .FB(d_register_1_fb));  // open: nQ
  Hex_Digit_Display #(.decimalPoint("false")) hex_digit_display_6 (.value(d_register_1_q));
  DEMUX demux_1 (.in_1({d_register_1_q_2, d_register_1_q}), .S(s_out), .CLK(CLK), .B(demux_1_b));  // open: A
  DEMUX demux_2 (.in_1(demux_1_b), .S(s_BUS_SEL), .CLK(CLK), .A(AD_BUS_O), .B(D_BUS_O));

  // Other names for the same wires on the sheet: bs = s_BUS_SEL; c = CLK
endmodule
